// Logisim project clock.circ as structural Verilog: 11 circuits, main circuit main
module main (
);

  wire am_pm_representation_1_a, am_pm_representation_1_b, am_pm_representation_1_c,
       am_pm_representation_1_d, am_pm_representation_1_e, am_pm_representation_1_f,
       am_pm_representation_1_g, and_1_out, and_2_out, and_3_out, and_4_out, clock_1_out, enable_out,
       hour_bcd_representation_1_b00, hour_bcd_representation_1_b01, hour_bcd_representation_1_b02,
       hour_bcd_representation_1_b03, hour_bcd_representation_1_b10, hour_bcd_representation_1_b11,
       hour_bcd_representation_1_b12, hour_bcd_representation_1_b13, n6_bcd_counter_1__5_recogniser,
       n6_bcd_counter_1_msb0, n6_bcd_counter_1_out_6, n6_bcd_counter_1_out_7, n6_bcd_counter_1_out_8,
       n6_bcd_counter_2__5_recogniser, n6_bcd_counter_2_msb0, n6_bcd_counter_2_out_6, n6_bcd_counter_2_out_7,
       n6_bcd_counter_2_out_8, n10_bcd_counter_1__0, n10_bcd_counter_1__1, n10_bcd_counter_1__2,
       n10_bcd_counter_1__3, n10_bcd_counter_1__9, n10_bcd_counter_2__0, n10_bcd_counter_2__1,
       n10_bcd_counter_2__2, n10_bcd_counter_2__3, n10_bcd_counter_2__9, n12_hr_counter_1__0,
       n12_hr_counter_1__1, n12_hr_counter_1__2, n12_hr_counter_1__3, n12_hr_counter_1_meridian, nor_1_out,
       or_1_out, reset_out, seven_segment_1_a, seven_segment_1_b, seven_segment_1_c, seven_segment_1_d,
       seven_segment_1_e, seven_segment_1_f, seven_segment_1_g, seven_segment_2_a, seven_segment_2_b,
       seven_segment_2_c, seven_segment_2_d, seven_segment_2_e, seven_segment_2_f, seven_segment_2_g,
       seven_segment_3_a, seven_segment_3_b, seven_segment_3_c, seven_segment_3_d, seven_segment_3_e,
       seven_segment_3_f, seven_segment_3_g, seven_segment_4_a, seven_segment_4_b, seven_segment_4_c,
       seven_segment_4_d, seven_segment_4_e, seven_segment_4_f, seven_segment_4_g, seven_segment_5_a,
       seven_segment_5_b, seven_segment_5_c, seven_segment_5_d, seven_segment_5_e, seven_segment_5_f,
       seven_segment_5_g, seven_segment_6_a, seven_segment_6_b, seven_segment_6_c, seven_segment_6_d,
       seven_segment_6_e, seven_segment_6_f, seven_segment_6_g;

  Clock clock_1 (.out(clock_1_out));
  Button enable (.out(enable_out));
  Button reset (.out(reset_out));
  or or_1 (or_1_out, reset_out, nor_1_out);
  and and_1 (and_1_out, enable_out, n10_bcd_counter_1__9);
  nor nor_1 (nor_1_out, n12_hr_counter_1__0, n12_hr_counter_1__1, n12_hr_counter_1__2, n12_hr_counter_1__3);
  _12_hr_counter u_12_hr_counter_1 (
    .clock(clock_1_out), .enable(and_4_out), .reset(or_1_out), ._3(n12_hr_counter_1__3),
    ._2(n12_hr_counter_1__2), ._1(n12_hr_counter_1__1), ._0(n12_hr_counter_1__0),
    .meridian(n12_hr_counter_1_meridian));
  _10_bcd_counter u_10_bcd_counter_1 (
    .clock(clock_1_out), .enable(enable_out), .reset(reset_out), ._9(n10_bcd_counter_1__9),
    ._0(n10_bcd_counter_1__0), ._1(n10_bcd_counter_1__1), ._2(n10_bcd_counter_1__2), ._3(n10_bcd_counter_1__3));
  _6_bcd_counter u_6_bcd_counter_1 (
    .clock(clock_1_out), .enable(and_1_out), .reset(reset_out), .MSB0(n6_bcd_counter_1_msb0),
    ._5_recogniser(n6_bcd_counter_1__5_recogniser), .out_6(n6_bcd_counter_1_out_6),
    .out_7(n6_bcd_counter_1_out_7), .out_8(n6_bcd_counter_1_out_8));
  hour_bcd_representation hour_bcd_representation_1 (
    .a0(n12_hr_counter_1__3), .a1(n12_hr_counter_1__2), .a2(n12_hr_counter_1__1), .a3(n12_hr_counter_1__0),
    .b00(hour_bcd_representation_1_b00), .b01(hour_bcd_representation_1_b01),
    .b02(hour_bcd_representation_1_b02), .b03(hour_bcd_representation_1_b03),
    .b10(hour_bcd_representation_1_b10), .b11(hour_bcd_representation_1_b11),
    .b12(hour_bcd_representation_1_b12), .b13(hour_bcd_representation_1_b13));
  seven_segment seven_segment_1 (
    .in1(n10_bcd_counter_1__0), .in2(n10_bcd_counter_1__1), .in3(n10_bcd_counter_1__2),
    .in4(n10_bcd_counter_1__3), .a(seven_segment_1_a), .b(seven_segment_1_b), .c(seven_segment_1_c),
    .d(seven_segment_1_d), .e(seven_segment_1_e), .f(seven_segment_1_f), .g(seven_segment_1_g));
  seven_segment seven_segment_2 (
    .in1(n6_bcd_counter_1_msb0), .in2(n6_bcd_counter_1_out_6), .in3(n6_bcd_counter_1_out_7),
    .in4(n6_bcd_counter_1_out_8), .a(seven_segment_2_a), .b(seven_segment_2_b), .c(seven_segment_2_c),
    .d(seven_segment_2_d), .e(seven_segment_2_e), .f(seven_segment_2_f), .g(seven_segment_2_g));
  and and_2 (and_2_out, n6_bcd_counter_1__5_recogniser, enable_out, and_1_out);
  _7_Segment_Display u_7_segment_display_1 (.f(1'b1), .a(1'b1), .e(1'b1), .d(1'b1));  // open: g, b, c, dp
  seven_segment seven_segment_3 (
    .in1(hour_bcd_representation_1_b00), .in2(hour_bcd_representation_1_b01),
    .in3(hour_bcd_representation_1_b02), .in4(hour_bcd_representation_1_b03), .a(seven_segment_3_a),
    .b(seven_segment_3_b), .c(seven_segment_3_c), .d(seven_segment_3_d), .e(seven_segment_3_e),
    .f(seven_segment_3_f), .g(seven_segment_3_g));
  seven_segment seven_segment_4 (
    .in1(hour_bcd_representation_1_b10), .in2(hour_bcd_representation_1_b11),
    .in3(hour_bcd_representation_1_b12), .in4(hour_bcd_representation_1_b13), .a(seven_segment_4_a),
    .b(seven_segment_4_b), .c(seven_segment_4_c), .d(seven_segment_4_d), .e(seven_segment_4_e),
    .f(seven_segment_4_f), .g(seven_segment_4_g));
  _7_Segment_Display u_7_segment_display_2 (.g(1'b1), .a(1'b1), .b(1'b1), .e(1'b1), .d(1'b1));  // open: f, c, dp
  _7_Segment_Display u_7_segment_display_3 (.g(1'b1), .f(1'b1), .a(1'b1), .d(1'b1), .c(1'b1));  // open: b, e, dp
  _7_Segment_Display u_7_segment_display_4 (
    .g(seven_segment_3_g), .f(seven_segment_3_f), .a(seven_segment_3_a), .b(seven_segment_3_b),
    .e(seven_segment_3_e), .d(seven_segment_3_d), .c(seven_segment_3_c));  // open: dp
  _7_Segment_Display u_7_segment_display_5 (
    .g(seven_segment_4_g), .f(seven_segment_4_f), .a(seven_segment_4_a), .b(seven_segment_4_b),
    .e(seven_segment_4_e), .d(seven_segment_4_d), .c(seven_segment_4_c), .dp(1'b1));
  _7_Segment_Display u_7_segment_display_6 (.b(1'b1), .c(1'b1));  // open: g, f, a, e, d, dp
  _7_Segment_Display u_7_segment_display_7 (
    .g(1'b1), .f(1'b1), .a(1'b1), .b(1'b1), .e(1'b1), .d(1'b1), .c(1'b1));  // open: dp
  _7_Segment_Display u_7_segment_display_8 (
    .g(seven_segment_6_g), .f(seven_segment_6_f), .a(seven_segment_6_a), .b(seven_segment_6_b),
    .e(seven_segment_6_e), .d(seven_segment_6_d), .c(seven_segment_6_c));  // open: dp
  _7_Segment_Display u_7_segment_display_9 (.g(1'b1), .a(1'b1), .b(1'b1), .d(1'b1), .c(1'b1));  // open: f, e, dp
  _7_Segment_Display u_7_segment_display_10 (
    .f(1'b1), .a(1'b1), .b(1'b1), .e(1'b1), .d(1'b1), .c(1'b1));  // open: g, dp
  _7_Segment_Display u_7_segment_display_11 (
    .g(seven_segment_5_g), .f(seven_segment_5_f), .a(seven_segment_5_a), .b(seven_segment_5_b),
    .e(seven_segment_5_e), .d(seven_segment_5_d), .c(seven_segment_5_c), .dp(1'b1));
  _10_bcd_counter u_10_bcd_counter_2 (
    .clock(clock_1_out), .enable(and_2_out), .reset(reset_out), ._9(n10_bcd_counter_2__9),
    ._0(n10_bcd_counter_2__0), ._1(n10_bcd_counter_2__1), ._2(n10_bcd_counter_2__2), ._3(n10_bcd_counter_2__3));
  _7_Segment_Display u_7_segment_display_12 (
    .f(1'b1), .a(1'b1), .b(1'b1), .e(1'b1), .d(1'b1), .c(1'b1), .dp(1'b1));  // open: g
  _7_Segment_Display u_7_segment_display_13 (
    .g(seven_segment_1_g), .f(seven_segment_1_f), .a(seven_segment_1_a), .b(seven_segment_1_b),
    .e(seven_segment_1_e), .d(seven_segment_1_d), .c(seven_segment_1_c), .dp(1'b1));
  _7_Segment_Display u_7_segment_display_14 (
    .g(seven_segment_2_g), .f(seven_segment_2_f), .a(seven_segment_2_a), .b(seven_segment_2_b),
    .e(seven_segment_2_e), .d(seven_segment_2_d), .c(seven_segment_2_c));  // open: dp
  and and_3 (and_3_out, n10_bcd_counter_2__9, and_2_out);
  am_pm_representation am_pm_representation_1 (
    .\input (n12_hr_counter_1_meridian), .a(am_pm_representation_1_a), .b(am_pm_representation_1_b),
    .c(am_pm_representation_1_c), .d(am_pm_representation_1_d), .e(am_pm_representation_1_e),
    .f(am_pm_representation_1_f), .g(am_pm_representation_1_g));
  _7_Segment_Display u_7_segment_display_15 (.f(1'b1), .a(1'b1), .b(1'b1), .e(1'b1), .c(1'b1));  // open: g, d, dp
  _7_Segment_Display u_7_segment_display_16 (
    .g(am_pm_representation_1_g), .f(am_pm_representation_1_f), .a(am_pm_representation_1_a),
    .b(am_pm_representation_1_b), .e(am_pm_representation_1_e), .d(am_pm_representation_1_d),
    .c(am_pm_representation_1_c));  // open: dp
  _6_bcd_counter u_6_bcd_counter_2 (
    .clock(clock_1_out), .enable(and_3_out), .reset(reset_out), .MSB0(n6_bcd_counter_2_msb0),
    ._5_recogniser(n6_bcd_counter_2__5_recogniser), .out_6(n6_bcd_counter_2_out_6),
    .out_7(n6_bcd_counter_2_out_7), .out_8(n6_bcd_counter_2_out_8));
  seven_segment seven_segment_5 (
    .in1(n10_bcd_counter_2__0), .in2(n10_bcd_counter_2__1), .in3(n10_bcd_counter_2__2),
    .in4(n10_bcd_counter_2__3), .a(seven_segment_5_a), .b(seven_segment_5_b), .c(seven_segment_5_c),
    .d(seven_segment_5_d), .e(seven_segment_5_e), .f(seven_segment_5_f), .g(seven_segment_5_g));
  seven_segment seven_segment_6 (
    .in1(n6_bcd_counter_2_msb0), .in2(n6_bcd_counter_2_out_6), .in3(n6_bcd_counter_2_out_7),
    .in4(n6_bcd_counter_2_out_8), .a(seven_segment_6_a), .b(seven_segment_6_b), .c(seven_segment_6_c),
    .d(seven_segment_6_d), .e(seven_segment_6_e), .f(seven_segment_6_f), .g(seven_segment_6_g));
  and and_4 (and_4_out, n6_bcd_counter_2__5_recogniser, and_3_out);
endmodule

module Main (
  input  in_1
);

  wire am_pm_representation_1_a, am_pm_representation_1_b, am_pm_representation_1_c,
       am_pm_representation_1_d, am_pm_representation_1_e, am_pm_representation_1_f,
       am_pm_representation_1_g, and_1_out, and_2_out, and_3_out, button_1_out, clock_1_out,
       hour_bcd_representation_1_b00, hour_bcd_representation_1_b01, hour_bcd_representation_1_b02,
       hour_bcd_representation_1_b03, hour_bcd_representation_1_b10, hour_bcd_representation_1_b11,
       hour_bcd_representation_1_b12, hour_bcd_representation_1_b13, n6_bcd_counter_1__5_recogniser,
       n6_bcd_counter_1_msb0, n6_bcd_counter_1_out_6, n6_bcd_counter_1_out_7, n6_bcd_counter_1_out_8,
       n6_bcd_counter_2__5_recogniser, n6_bcd_counter_2_msb0, n6_bcd_counter_2_out_6, n6_bcd_counter_2_out_7,
       n6_bcd_counter_2_out_8, n10_bcd_counter_1__0, n10_bcd_counter_1__1, n10_bcd_counter_1__2,
       n10_bcd_counter_1__3, n10_bcd_counter_1__9, n10_bcd_counter_2__0, n10_bcd_counter_2__1,
       n10_bcd_counter_2__2, n10_bcd_counter_2__3, n10_bcd_counter_2__9, n12_hr_counter_1__0,
       n12_hr_counter_1__1, n12_hr_counter_1__2, n12_hr_counter_1__3, n12_hr_counter_1_meridian, nor_1_out,
       not_1_out, or_1_out, seven_segment_1_a, seven_segment_1_b, seven_segment_1_c, seven_segment_1_d,
       seven_segment_1_e, seven_segment_1_f, seven_segment_1_g, seven_segment_2_a, seven_segment_2_b,
       seven_segment_2_c, seven_segment_2_d, seven_segment_2_e, seven_segment_2_f, seven_segment_2_g,
       seven_segment_3_a, seven_segment_3_b, seven_segment_3_c, seven_segment_3_d, seven_segment_3_e,
       seven_segment_3_f, seven_segment_3_g, seven_segment_4_a, seven_segment_4_b, seven_segment_4_c,
       seven_segment_4_d, seven_segment_4_e, seven_segment_4_f, seven_segment_4_g, seven_segment_5_a,
       seven_segment_5_b, seven_segment_5_c, seven_segment_5_d, seven_segment_5_e, seven_segment_5_f,
       seven_segment_5_g, seven_segment_6_a, seven_segment_6_b, seven_segment_6_c, seven_segment_6_d,
       seven_segment_6_e, seven_segment_6_f, seven_segment_6_g;

  Clock clock_1 (.out(clock_1_out));
  not not_1 (not_1_out, in_1);
  Button button_1 (.out(button_1_out));
  or or_1 (or_1_out, button_1_out, nor_1_out);
  nor nor_1 (nor_1_out, n12_hr_counter_1__0, n12_hr_counter_1__1, n12_hr_counter_1__2, n12_hr_counter_1__3);
  _12_hr_counter u_12_hr_counter_1 (
    .clock(clock_1_out), .enable(and_3_out), .reset(or_1_out), ._3(n12_hr_counter_1__3),
    ._2(n12_hr_counter_1__2), ._1(n12_hr_counter_1__1), ._0(n12_hr_counter_1__0),
    .meridian(n12_hr_counter_1_meridian));
  _10_bcd_counter u_10_bcd_counter_1 (
    .clock(clock_1_out), .enable(not_1_out), .reset(button_1_out), ._9(n10_bcd_counter_1__9),
    ._0(n10_bcd_counter_1__0), ._1(n10_bcd_counter_1__1), ._2(n10_bcd_counter_1__2), ._3(n10_bcd_counter_1__3));
  _6_bcd_counter u_6_bcd_counter_1 (
    .clock(clock_1_out), .enable(n10_bcd_counter_1__9), .reset(button_1_out), .MSB0(n6_bcd_counter_1_msb0),
    ._5_recogniser(n6_bcd_counter_1__5_recogniser), .out_6(n6_bcd_counter_1_out_6),
    .out_7(n6_bcd_counter_1_out_7), .out_8(n6_bcd_counter_1_out_8));
  hour_bcd_representation hour_bcd_representation_1 (
    .a0(n12_hr_counter_1__3), .a1(n12_hr_counter_1__2), .a2(n12_hr_counter_1__1), .a3(n12_hr_counter_1__0),
    .b00(hour_bcd_representation_1_b00), .b01(hour_bcd_representation_1_b01),
    .b02(hour_bcd_representation_1_b02), .b03(hour_bcd_representation_1_b03),
    .b10(hour_bcd_representation_1_b10), .b11(hour_bcd_representation_1_b11),
    .b12(hour_bcd_representation_1_b12), .b13(hour_bcd_representation_1_b13));
  seven_segment seven_segment_1 (
    .in1(n10_bcd_counter_1__0), .in2(n10_bcd_counter_1__1), .in3(n10_bcd_counter_1__2),
    .in4(n10_bcd_counter_1__3), .a(seven_segment_1_a), .b(seven_segment_1_b), .c(seven_segment_1_c),
    .d(seven_segment_1_d), .e(seven_segment_1_e), .f(seven_segment_1_f), .g(seven_segment_1_g));
  seven_segment seven_segment_2 (
    .in1(n6_bcd_counter_1_msb0), .in2(n6_bcd_counter_1_out_6), .in3(n6_bcd_counter_1_out_7),
    .in4(n6_bcd_counter_1_out_8), .a(seven_segment_2_a), .b(seven_segment_2_b), .c(seven_segment_2_c),
    .d(seven_segment_2_d), .e(seven_segment_2_e), .f(seven_segment_2_f), .g(seven_segment_2_g));
  and and_1 (and_1_out, n6_bcd_counter_1__5_recogniser, not_1_out, n10_bcd_counter_1__9);
  _7_Segment_Display u_7_segment_display_1 (.f(1'b1), .a(1'b1), .e(1'b1), .d(1'b1));  // open: g, b, c, dp
  seven_segment seven_segment_3 (
    .in1(hour_bcd_representation_1_b00), .in2(hour_bcd_representation_1_b01),
    .in3(hour_bcd_representation_1_b02), .in4(hour_bcd_representation_1_b03), .a(seven_segment_3_a),
    .b(seven_segment_3_b), .c(seven_segment_3_c), .d(seven_segment_3_d), .e(seven_segment_3_e),
    .f(seven_segment_3_f), .g(seven_segment_3_g));
  seven_segment seven_segment_4 (
    .in1(hour_bcd_representation_1_b10), .in2(hour_bcd_representation_1_b11),
    .in3(hour_bcd_representation_1_b12), .in4(hour_bcd_representation_1_b13), .a(seven_segment_4_a),
    .b(seven_segment_4_b), .c(seven_segment_4_c), .d(seven_segment_4_d), .e(seven_segment_4_e),
    .f(seven_segment_4_f), .g(seven_segment_4_g));
  _7_Segment_Display u_7_segment_display_2 (.g(1'b1), .a(1'b1), .b(1'b1), .e(1'b1), .d(1'b1));  // open: f, c, dp
  _7_Segment_Display u_7_segment_display_3 (.g(1'b1), .f(1'b1), .a(1'b1), .d(1'b1), .c(1'b1));  // open: b, e, dp
  _7_Segment_Display u_7_segment_display_4 (
    .g(seven_segment_3_g), .f(seven_segment_3_f), .a(seven_segment_3_a), .b(seven_segment_3_b),
    .e(seven_segment_3_e), .d(seven_segment_3_d), .c(seven_segment_3_c));  // open: dp
  _7_Segment_Display u_7_segment_display_5 (
    .g(seven_segment_4_g), .f(seven_segment_4_f), .a(seven_segment_4_a), .b(seven_segment_4_b),
    .e(seven_segment_4_e), .d(seven_segment_4_d), .c(seven_segment_4_c), .dp(1'b1));
  _7_Segment_Display u_7_segment_display_6 (
    .g(1'b1), .f(1'b1), .a(1'b1), .b(1'b1), .e(1'b1), .d(1'b1), .c(1'b1));  // open: dp
  _7_Segment_Display u_7_segment_display_7 (.b(1'b1), .c(1'b1));  // open: g, f, a, e, d, dp
  _7_Segment_Display u_7_segment_display_8 (
    .g(seven_segment_6_g), .f(seven_segment_6_f), .a(seven_segment_6_a), .b(seven_segment_6_b),
    .e(seven_segment_6_e), .d(seven_segment_6_d), .c(seven_segment_6_c));  // open: dp
  _7_Segment_Display u_7_segment_display_9 (.f(1'b1), .a(1'b1), .b(1'b1), .e(1'b1), .d(1'b1), .c(1'b1));  // open: g, dp
  _7_Segment_Display u_7_segment_display_10 (.g(1'b1), .a(1'b1), .b(1'b1), .d(1'b1), .c(1'b1));  // open: f, e, dp
  _7_Segment_Display u_7_segment_display_11 (
    .g(seven_segment_5_g), .f(seven_segment_5_f), .a(seven_segment_5_a), .b(seven_segment_5_b),
    .e(seven_segment_5_e), .d(seven_segment_5_d), .c(seven_segment_5_c), .dp(1'b1));
  _10_bcd_counter u_10_bcd_counter_2 (
    .clock(clock_1_out), .enable(and_1_out), .reset(button_1_out), ._9(n10_bcd_counter_2__9),
    ._0(n10_bcd_counter_2__0), ._1(n10_bcd_counter_2__1), ._2(n10_bcd_counter_2__2), ._3(n10_bcd_counter_2__3));
  _7_Segment_Display u_7_segment_display_12 (
    .f(1'b1), .a(1'b1), .b(1'b1), .e(1'b1), .d(1'b1), .c(1'b1), .dp(1'b1));  // open: g
  _7_Segment_Display u_7_segment_display_13 (
    .g(seven_segment_2_g), .f(seven_segment_2_f), .a(seven_segment_2_a), .b(seven_segment_2_b),
    .e(seven_segment_2_e), .d(seven_segment_2_d), .c(seven_segment_2_c));  // open: dp
  _7_Segment_Display u_7_segment_display_14 (
    .g(seven_segment_1_g), .f(seven_segment_1_f), .a(seven_segment_1_a), .b(seven_segment_1_b),
    .e(seven_segment_1_e), .d(seven_segment_1_d), .c(seven_segment_1_c), .dp(1'b1));
  and and_2 (and_2_out, n10_bcd_counter_2__9, and_1_out);
  am_pm_representation am_pm_representation_1 (
    .\input (n12_hr_counter_1_meridian), .a(am_pm_representation_1_a), .b(am_pm_representation_1_b),
    .c(am_pm_representation_1_c), .d(am_pm_representation_1_d), .e(am_pm_representation_1_e),
    .f(am_pm_representation_1_f), .g(am_pm_representation_1_g));
  _7_Segment_Display u_7_segment_display_15 (
    .g(am_pm_representation_1_g), .f(am_pm_representation_1_f), .a(am_pm_representation_1_a),
    .b(am_pm_representation_1_b), .e(am_pm_representation_1_e), .d(am_pm_representation_1_d),
    .c(am_pm_representation_1_c));  // open: dp
  _7_Segment_Display u_7_segment_display_16 (.f(1'b1), .a(1'b1), .b(1'b1), .e(1'b1), .c(1'b1));  // open: g, d, dp
  _6_bcd_counter u_6_bcd_counter_2 (
    .clock(clock_1_out), .enable(and_2_out), .reset(button_1_out), .MSB0(n6_bcd_counter_2_msb0),
    ._5_recogniser(n6_bcd_counter_2__5_recogniser), .out_6(n6_bcd_counter_2_out_6),
    .out_7(n6_bcd_counter_2_out_7), .out_8(n6_bcd_counter_2_out_8));
  seven_segment seven_segment_5 (
    .in1(n10_bcd_counter_2__0), .in2(n10_bcd_counter_2__1), .in3(n10_bcd_counter_2__2),
    .in4(n10_bcd_counter_2__3), .a(seven_segment_5_a), .b(seven_segment_5_b), .c(seven_segment_5_c),
    .d(seven_segment_5_d), .e(seven_segment_5_e), .f(seven_segment_5_f), .g(seven_segment_5_g));
  seven_segment seven_segment_6 (
    .in1(n6_bcd_counter_2_msb0), .in2(n6_bcd_counter_2_out_6), .in3(n6_bcd_counter_2_out_7),
    .in4(n6_bcd_counter_2_out_8), .a(seven_segment_6_a), .b(seven_segment_6_b), .c(seven_segment_6_c),
    .d(seven_segment_6_d), .e(seven_segment_6_e), .f(seven_segment_6_f), .g(seven_segment_6_g));
  and and_3 (and_3_out, n6_bcd_counter_2__5_recogniser, and_2_out);
endmodule

module seven_segment (
  input  in1,
  input  in2,
  input  in3,
  input  in4,
  output a,
  output b,
  output c,
  output d,
  output e,
  output f,
  output g
);

  wire and_1_out, and_2_out, and_3_out, and_4_out, and_5_out, and_6_out, and_7_out, and_8_out, and_9_out,
       and_10_out, and_11_out, and_12_out, and_13_out, and_14_out, and_15_out, and_16_out, and_17_out,
       not_1_out, not_2_out, not_3_out, not_4_out, not_5_out, not_6_out, not_7_out, not_8_out, not_9_out,
       not_10_out, not_11_out, not_12_out, not_13_out, not_14_out, not_15_out, not_16_out, not_17_out,
       not_18_out, not_19_out, not_20_out, not_21_out, or_1_out, or_2_out, or_3_out, or_4_out, or_6_out,
       or_8_out, or_9_out, or_10_out, or_11_out, or_14_out, or_15_out;

  not not_1 (not_1_out, in2);
  and and_1 (and_1_out, not_1_out, not_2_out);
  not not_2 (not_2_out, in4);
  and and_2 (and_2_out, in2, in4);
  not not_3 (not_3_out, in2);
  not not_4 (not_4_out, in3);
  and and_3 (and_3_out, not_4_out, not_5_out);
  not not_5 (not_5_out, in4);
  not not_6 (not_6_out, in3);
  or or_1 (or_1_out, not_6_out, in4);
  not not_7 (not_7_out, in2);
  and and_4 (and_4_out, not_7_out, not_8_out);
  not not_8 (not_8_out, in4);
  not not_9 (not_9_out, in2);
  and and_5 (and_5_out, not_9_out, in3);
  not not_10 (not_10_out, in4);
  and and_6 (and_6_out, in2, not_11_out);
  not not_11 (not_11_out, in3);
  not not_12 (not_12_out, in2);
  and and_7 (and_7_out, not_12_out, not_13_out);
  not not_13 (not_13_out, in4);
  and and_8 (and_8_out, in3, not_14_out);
  not not_14 (not_14_out, in4);
  not not_15 (not_15_out, in3);
  and and_9 (and_9_out, not_15_out, not_16_out);
  not not_16 (not_16_out, in4);
  and and_10 (and_10_out, in2, not_17_out);
  not not_17 (not_17_out, in3);
  and and_11 (and_11_out, in2, not_18_out);
  not not_18 (not_18_out, in4);
  not not_19 (not_19_out, in2);
  and and_12 (and_12_out, not_19_out, in3);
  and and_13 (and_13_out, in2, not_20_out);
  not not_20 (not_20_out, in3);
  and and_14 (and_14_out, in2, not_21_out);
  not not_21 (not_21_out, in4);
  or or_2 (or_2_out, and_1_out, in3);
  or or_3 (or_3_out, and_2_out, in1);
  or or_4 (or_4_out, not_3_out, and_3_out);
  and and_15 (and_15_out, in3, in4);
  or or_5 (c, or_1_out, in2);
  or or_6 (or_6_out, and_4_out, and_5_out);
  and and_16 (and_16_out, in3, not_10_out);
  and and_17 (and_17_out, and_6_out, in4);
  or or_7 (e, and_7_out, and_8_out);
  or or_8 (or_8_out, and_9_out, and_10_out);
  or or_9 (or_9_out, and_11_out, in1);
  or or_10 (or_10_out, and_12_out, and_13_out);
  or or_11 (or_11_out, and_14_out, in1);
  or or_12 (a, or_2_out, or_3_out);
  or or_13 (b, or_4_out, and_15_out);
  or or_14 (or_14_out, or_6_out, and_16_out);
  or or_15 (or_15_out, and_17_out, in1);
  or or_16 (f, or_8_out, or_9_out);
  or or_17 (g, or_10_out, or_11_out);
  or or_18 (d, or_14_out, or_15_out);
endmodule

module _10_bcd_counter (
  input  clock,
  input  enable,
  input  reset,
  output _9,
  output _0,
  output _1,
  output _2,
  output _3
);

  wire comb_10counter_1_q0_, comb_10counter_1_q1_, comb_10counter_1_q2_, comb_10counter_1_q3_, not_1_out,
       not_2_out;

  D_Flip_Flop d_ff_1 (.clk(clock), .D(comb_10counter_1_q0_), .Q(_0), .en(enable), .reset(reset));  // open: Qn, preset
  comb_10counter comb_10counter_1 (
    .q0(_0), .q1(_1), .q2(_2), .q3(_3), .q0_(comb_10counter_1_q0_), .q1_(comb_10counter_1_q1_),
    .q2_(comb_10counter_1_q2_), .q3_(comb_10counter_1_q3_));
  D_Flip_Flop d_ff_2 (.clk(clock), .D(comb_10counter_1_q1_), .Q(_1), .en(enable), .reset(reset));  // open: Qn, preset
  D_Flip_Flop d_ff_3 (.clk(clock), .D(comb_10counter_1_q2_), .Q(_2), .en(enable), .reset(reset));  // open: Qn, preset
  D_Flip_Flop d_ff_4 (.clk(clock), .D(comb_10counter_1_q3_), .Q(_3), .en(enable), .reset(reset));  // open: Qn, preset
  not not_1 (not_1_out, _2);
  not not_2 (not_2_out, _1);
  and and_1 (_9, _3, not_1_out, not_2_out, _0);
endmodule

module comb_10counter (
  input  q0,
  input  q1,
  input  q2,
  input  q3,
  output q0_,
  output q1_,
  output q2_,
  output q3_
);

  wire and_1_out, and_2_out, and_3_out, and_4_out, and_5_out, and_6_out, and_7_out, not_1_out, not_2_out,
       not_3_out, not_4_out, not_5_out, not_6_out, not_7_out;

  and and_1 (and_1_out, q1, q2, q3);
  and and_2 (and_2_out, q0, not_1_out);
  not not_1 (not_1_out, q3);
  not not_2 (not_2_out, q1);
  and and_3 (and_3_out, not_2_out, q2, q3);
  and and_4 (and_4_out, q1, not_3_out);
  not not_3 (not_3_out, q2);
  and and_5 (and_5_out, q1, not_4_out);
  not not_4 (not_4_out, q3);
  not not_5 (not_5_out, q0);
  not not_6 (not_6_out, q2);
  and and_6 (and_6_out, not_5_out, not_6_out, q3);
  and and_7 (and_7_out, q2, not_7_out);
  not not_7 (not_7_out, q3);
  not not_8 (q3_, q3);
  or or_1 (q0_, and_1_out, and_2_out);
  or or_2 (q1_, and_3_out, and_4_out, and_5_out);
  or or_3 (q2_, and_6_out, and_7_out);
endmodule

module _6_bcd_counter (
  input  clock,
  input  enable,
  input  reset,
  output MSB0,
  output _5_recogniser,
  output out_6,
  output out_7,
  output out_8
);

  wire comb_6_counter_1_q0_, comb_6_counter_1_q1_, comb_6_counter_1_q2_, not_1_out;

  D_Flip_Flop d_ff_1 (
    .clk(clock), .D(comb_6_counter_1_q0_), .Q(out_6), .en(enable), .reset(reset));  // open: Qn, preset
  comb_6_counter comb_6_counter_1 (
    .q0(out_6), .q1(out_7), .q2(out_8), .q0_(comb_6_counter_1_q0_), .q1_(comb_6_counter_1_q1_),
    .q2_(comb_6_counter_1_q2_));
  D_Flip_Flop d_ff_2 (
    .clk(clock), .D(comb_6_counter_1_q1_), .Q(out_7), .en(enable), .reset(reset));  // open: Qn, preset
  D_Flip_Flop d_ff_3 (
    .clk(clock), .D(comb_6_counter_1_q2_), .Q(out_8), .en(enable), .reset(reset));  // open: Qn, preset
  not not_1 (not_1_out, out_7);
  and and_1 (_5_recogniser, out_8, not_1_out, out_6);

  assign MSB0 = 1'b0;
endmodule

module comb_6_counter (
  input  q0,
  input  q1,
  input  q2,
  output q0_,
  output q1_,
  output q2_
);

  wire and_1_out, and_2_out, and_3_out, and_4_out, not_1_out, not_2_out, not_3_out, not_4_out;

  not not_1 (not_1_out, q2);
  not not_2 (not_2_out, q0);
  not not_3 (not_3_out, q1);
  not not_4 (not_4_out, q2);
  not not_5 (q2_, q2);
  and and_1 (and_1_out, q1, q2);
  and and_2 (and_2_out, q0, not_1_out);
  and and_3 (and_3_out, not_2_out, not_3_out, q2);
  and and_4 (and_4_out, q1, not_4_out);
  or or_1 (q0_, and_1_out, and_2_out);
  or or_2 (q1_, and_3_out, and_4_out);
endmodule

module _12_hr_counter (
  input  clock,
  input  enable,
  input  reset,
  output _3,
  output _2,
  output _1,
  output _0,
  output meridian
);

  wire n12_hr_combo_circuit_1_meridian_, n12_hr_combo_circuit_1_q0_, n12_hr_combo_circuit_1_q1_,
       n12_hr_combo_circuit_1_q2_, n12_hr_combo_circuit_1_q3_;

  D_Flip_Flop d_ff_1 (
    .clk(clock), .D(n12_hr_combo_circuit_1_meridian_), .Q(meridian), .en(enable), .reset(reset));  // open: Qn, preset
  D_Flip_Flop d_ff_2 (
    .clk(clock), .D(n12_hr_combo_circuit_1_q0_), .Q(_3), .preset(reset), .en(enable));  // open: Qn, reset
  _12_hr_combo_circuit u_12_hr_combo_circuit_1 (
    .meridian(meridian), .q0(_3), .q1(_2), .q2(_1), .q3(_0), .meridian_(n12_hr_combo_circuit_1_meridian_),
    .q0_(n12_hr_combo_circuit_1_q0_), .q1_(n12_hr_combo_circuit_1_q1_), .q2_(n12_hr_combo_circuit_1_q2_),
    .q3_(n12_hr_combo_circuit_1_q3_));
  D_Flip_Flop d_ff_3 (
    .clk(clock), .D(n12_hr_combo_circuit_1_q1_), .Q(_2), .preset(reset), .en(enable));  // open: Qn, reset
  D_Flip_Flop d_ff_4 (
    .clk(clock), .D(n12_hr_combo_circuit_1_q2_), .Q(_1), .en(enable), .reset(reset));  // open: Qn, preset
  D_Flip_Flop d_ff_5 (
    .clk(clock), .D(n12_hr_combo_circuit_1_q3_), .Q(_0), .en(enable), .reset(reset));  // open: Qn, preset
endmodule

module _12_hr_combo_circuit (
  input  meridian,
  input  q0,
  input  q1,
  input  q2,
  input  q3,
  output meridian_,
  output q0_,
  output q1_,
  output q2_,
  output q3_
);

  wire and_1_out, and_2_out, and_3_out, and_4_out, and_5_out, and_6_out, and_7_out, and_8_out, and_9_out,
       and_10_out, and_11_out, not_1_out, not_2_out, not_3_out, not_4_out, not_5_out, not_6_out, not_7_out,
       not_8_out, not_9_out, not_10_out, not_11_out, not_12_out;

  seven_segment seven_segment_1 ();  // open: in1, in2, in3, in4, a, b, c, d, e, f, g
  not not_1 (not_1_out, meridian);
  not not_2 (not_2_out, q0);
  not not_3 (not_3_out, q2);
  not not_4 (not_4_out, q3);
  not not_5 (not_5_out, q1);
  not not_6 (not_6_out, q1);
  not not_7 (not_7_out, q0);
  not not_8 (not_8_out, q2);
  not not_9 (not_9_out, q0);
  not not_10 (not_10_out, q3);
  not not_11 (not_11_out, q2);
  not not_12 (not_12_out, q3);
  not not_13 (q3_, q3);
  and and_1 (and_1_out, not_1_out, q0, q2, q3);
  and and_2 (and_2_out, meridian, not_2_out);
  and and_3 (and_3_out, meridian, not_3_out);
  and and_4 (and_4_out, meridian, not_4_out);
  and and_5 (and_5_out, q1, q2, q3);
  and and_6 (and_6_out, q0, not_5_out);
  and and_7 (and_7_out, not_6_out, q2, q3);
  and and_8 (and_8_out, not_7_out, q1, not_8_out);
  and and_9 (and_9_out, not_9_out, q1, not_10_out);
  and and_10 (and_10_out, not_11_out, q3);
  and and_11 (and_11_out, q2, not_12_out);
  or or_1 (meridian_, and_1_out, and_2_out, and_3_out, and_4_out);
  or or_2 (q0_, and_5_out, and_6_out);
  or or_3 (q1_, and_7_out, and_8_out, and_9_out);
  or or_4 (q2_, and_10_out, and_11_out);
  _7_Segment_Display u_7_segment_display_1 ();  // open: g, f, a, b, e, d, c, dp
endmodule

module hour_bcd_representation (
  input  a0,
  input  a1,
  input  a2,
  input  a3,
  output b00,
  output b01,
  output b02,
  output b03,
  output b10,
  output b11,
  output b12,
  output b13
);

  wire and_1_out, and_2_out, and_5_out, and_6_out, not_1_out, not_2_out, not_3_out, not_4_out;

  and and_1 (and_1_out, a0, a2);
  and and_2 (and_2_out, a0, a1);
  not not_1 (not_1_out, a1);
  and and_3 (b10, a0, not_1_out, not_2_out);
  not not_2 (not_2_out, a2);
  not not_3 (not_3_out, a0);
  and and_4 (b11, not_3_out, a1);
  not not_4 (not_4_out, a0);
  and and_5 (and_5_out, not_4_out, a2);
  and and_6 (and_6_out, a0, a1);
  or or_1 (b03, and_1_out, and_2_out);
  or or_2 (b12, and_5_out, and_6_out);

  assign b00 = 1'b0;
  assign b01 = 1'b0;
  assign b02 = 1'b0;
  assign b13 = a3;
endmodule

module am_pm_representation (
  input  \input ,
  output a,
  output b,
  output c,
  output d,
  output e,
  output f,
  output g
);

  not not_1 (c, \input );

  assign a = 1'b1;
  assign b = 1'b1;
  assign d = 1'b0;
  assign e = 1'b1;
  assign f = 1'b1;
  assign g = 1'b1;
endmodule
